// Logisim project circuito.circ as structural Verilog: 14 circuits, main circuit main
module main (
  input  in_1,
  input  in_2
);

  wire and_1_out, button_1_out, button_2_out, button_3_out, button_4_out, clock_1_out, not_1_out;
  wire [3:0] cronometro_1_dm, cronometro_1_ds, cronometro_1_um, cronometro_1_us, cronometro_2_dm,
       cronometro_2_ds, cronometro_2_um, cronometro_2_us, \preset_1_saída ;

  Clock clock_1 (.out(clock_1_out));
  Button button_1 (.out(button_1_out));
  and and_1 (and_1_out, clock_1_out, in_1);
  Hex_Digit_Display hex_digit_display_1 (.value(\preset_1_saída ));  // open: dp
  PRESET preset_1 (.CLK(button_1_out), .CLEAR(button_2_out), .\SAÍDA (\preset_1_saída ));
  Button button_2 (.out(button_2_out));
  Hex_Digit_Display hex_digit_display_2 (.value(cronometro_1_dm));  // open: dp
  Hex_Digit_Display hex_digit_display_3 (.value(cronometro_1_um));  // open: dp
  Button button_3 (.out(button_3_out));
  CRONOMETRO cronometro_1 (
    .CLK(and_1_out), .PRESET_DM(\preset_1_saída ), .DM(cronometro_1_dm), .UM(cronometro_1_um),
    .DS(cronometro_1_ds), .US(cronometro_1_us), .ENABLE(in_2), .ACTIVATE_PRESET(button_3_out),
    .CLEAR(button_4_out));
  Button button_4 (.out(button_4_out));
  Hex_Digit_Display hex_digit_display_4 (.value(cronometro_1_us));  // open: dp
  Hex_Digit_Display hex_digit_display_5 (.value(cronometro_1_ds));  // open: dp
  not not_1 (not_1_out, in_2);
  Hex_Digit_Display hex_digit_display_6 (.value(cronometro_2_dm));  // open: dp
  Hex_Digit_Display hex_digit_display_7 (.value(cronometro_2_um));  // open: dp
  CRONOMETRO cronometro_2 (
    .CLK(and_1_out), .PRESET_DM(\preset_1_saída ), .DM(cronometro_2_dm), .UM(cronometro_2_um),
    .DS(cronometro_2_ds), .US(cronometro_2_us), .ENABLE(not_1_out), .ACTIVATE_PRESET(button_3_out),
    .CLEAR(button_4_out));
  Hex_Digit_Display hex_digit_display_8 (.value(cronometro_2_ds));  // open: dp
  Hex_Digit_Display hex_digit_display_9 (.value(cronometro_2_us));  // open: dp
endmodule

module MUX (
  input  [3:0] A,
  input  [3:0] B,
  input  SELETOR,
  output [3:0] \SAÍDA 
);

  wire [3:0] \and_1_saída , \and_2_saída , \not_1_saída ;

  AND and_1 (.\SAÍDA (\and_1_saída ), .A(A), .B(\not_1_saída ));
  NOT not_1 (.A({4{SELETOR}}), .\SAÍDA (\not_1_saída ));
  AND and_2 (.\SAÍDA (\and_2_saída ), .A(B), .B({4{SELETOR}}));
  OR or_1 (.\SAÍDA (\SAÍDA ), .A(\and_1_saída ), .B(\and_2_saída ));
endmodule

module NOT (
  input  [3:0] A,
  output [3:0] \SAÍDA 
);

  not not_1 (\SAÍDA [0], A[0]);
  not not_2 (\SAÍDA [1], A[1]);
  not not_3 (\SAÍDA [2], A[2]);
  not not_4 (\SAÍDA [3], A[3]);
endmodule

module AND (
  input  [3:0] A,
  input  [3:0] B,
  output [3:0] \SAÍDA 
);

  and and_1 (\SAÍDA [0], B[0], A[0]);
  and and_2 (\SAÍDA [1], B[1], A[1]);
  and and_3 (\SAÍDA [2], B[2], A[2]);
  and and_4 (\SAÍDA [3], B[3], A[3]);
endmodule

module OR (
  input  [3:0] A,
  input  [3:0] B,
  output [3:0] \SAÍDA 
);

  or or_1 (\SAÍDA [0], B[0], A[0]);
  or or_2 (\SAÍDA [1], B[1], A[1]);
  or or_3 (\SAÍDA [2], B[2], A[2]);
  or or_4 (\SAÍDA [3], B[3], A[3]);
endmodule

// SUM
module SOMADOR (
  input  [3:0] A,
  input  [3:0] B,
  output [3:0] SUM,
  output CARRY
);

  wire and_1_out, and_2_out, and_3_out, and_4_out, and_5_out, and_6_out, and_7_out, and_8_out, and_9_out,
       and_10_out, and_11_out, and_12_out, or_1_out, or_2_out, or_3_out;

  and and_1 (and_1_out, A[0], B[0]);
  and and_2 (and_2_out, A[0], 1'b0);
  and and_3 (and_3_out, B[0], 1'b0);
  XOR xor_1 (.A(1'b0), .B(A[0]), .C(B[0]), .\SAÍDA (SUM[0]));
  or or_1 (or_1_out, and_1_out, and_2_out, and_3_out);
  XOR xor_2 (.A(or_1_out), .B(A[1]), .C(B[1]), .\SAÍDA (SUM[1]));
  and and_4 (and_4_out, A[1], B[1]);
  and and_5 (and_5_out, A[1], or_1_out);
  and and_6 (and_6_out, or_1_out, B[1]);
  or or_2 (or_2_out, and_4_out, and_5_out, and_6_out);
  XOR xor_3 (.A(or_2_out), .B(A[2]), .C(B[2]), .\SAÍDA (SUM[2]));
  and and_7 (and_7_out, A[2], B[2]);
  and and_8 (and_8_out, A[2], or_2_out);
  and and_9 (and_9_out, or_2_out, B[2]);
  or or_3 (or_3_out, and_7_out, and_8_out, and_9_out);
  XOR xor_4 (.A(or_3_out), .B(A[3]), .C(B[3]), .\SAÍDA (SUM[3]));
  and and_10 (and_10_out, A[3], B[3]);
  and and_11 (and_11_out, A[3], or_3_out);
  and and_12 (and_12_out, or_3_out, B[3]);
  or or_4 (CARRY, and_10_out, and_11_out, and_12_out);
endmodule

module XOR (
  input  A,
  input  B,
  input  C,
  output \SAÍDA 
);

  wire and_1_out, and_2_out, and_3_out, and_4_out, or_1_out;

  and and_1 (and_1_out, ~A, B);  // AND_Gate
  and and_2 (and_2_out, A, ~B);  // AND_Gate
  or or_1 (or_1_out, and_1_out, and_2_out);
  and and_3 (and_3_out, ~or_1_out, C);  // AND_Gate
  and and_4 (and_4_out, or_1_out, ~C);  // AND_Gate
  or or_2 (\SAÍDA , and_3_out, and_4_out);
endmodule

// FFD
module FLIP_FLOP_D (
  input  D,
  input  CLK,
  input  ENABLE,
  input  PRESET,
  input  CLEAR,
  output Q
);

  wire and_1_out, and_2_out, and_3_out, nor_2_out, not_1_out, not_2_out, not_3_out, not_4_out, or_1_out,
       or_2_out;

  not not_1 (not_1_out, CLK);
  not not_2 (not_2_out, not_3_out);
  not not_3 (not_3_out, not_1_out);
  and and_1 (and_1_out, not_2_out, CLK, ENABLE);
  not not_4 (not_4_out, D);
  and and_2 (and_2_out, not_4_out, and_1_out);
  and and_3 (and_3_out, and_1_out, D);
  or or_1 (or_1_out, CLEAR, and_2_out);
  or or_2 (or_2_out, and_3_out, PRESET);
  nor nor_1 (Q, or_1_out, nor_2_out);
  nor nor_2 (nor_2_out, Q, or_2_out);
endmodule

// REGIS
module REGISTRADOR (
  input  [3:0] D,
  input  CLK,
  input  ENABLE,
  input  CLEAR,
  input  ACTIVATE_PRESET,
  input  [3:0] PRESET,
  output [3:0] \SAÍDA 
);

  wire and_1_out, and_2_out, and_3_out, and_4_out, or_1_out, or_2_out, or_3_out, or_4_out;
  wire [3:0] \mux_1_saída ;

  FLIP_FLOP_D flip_flop_d_1 (
    .D(D[0]), .CLK(CLK), .ENABLE(ENABLE), .PRESET(\mux_1_saída [0]), .CLEAR(or_1_out), .Q(\SAÍDA [0]));
  or or_1 (or_1_out, and_1_out, CLEAR);
  and and_1 (and_1_out, ~\mux_1_saída [0], ACTIVATE_PRESET);  // AND_Gate
  FLIP_FLOP_D flip_flop_d_2 (
    .D(D[1]), .CLK(CLK), .ENABLE(ENABLE), .PRESET(\mux_1_saída [1]), .CLEAR(or_2_out), .Q(\SAÍDA [1]));
  or or_2 (or_2_out, and_2_out, CLEAR);
  and and_2 (and_2_out, ~\mux_1_saída [1], ACTIVATE_PRESET);  // AND_Gate
  MUX mux_1 (.A(4'b0000), .B(PRESET), .SELETOR(ACTIVATE_PRESET), .\SAÍDA (\mux_1_saída ));
  FLIP_FLOP_D flip_flop_d_3 (
    .D(D[2]), .CLK(CLK), .ENABLE(ENABLE), .PRESET(\mux_1_saída [2]), .CLEAR(or_3_out), .Q(\SAÍDA [2]));
  or or_3 (or_3_out, and_3_out, CLEAR);
  and and_3 (and_3_out, ~\mux_1_saída [2], ACTIVATE_PRESET);  // AND_Gate
  FLIP_FLOP_D flip_flop_d_4 (
    .D(D[3]), .CLK(CLK), .ENABLE(ENABLE), .PRESET(\mux_1_saída [3]), .CLEAR(or_4_out), .Q(\SAÍDA [3]));
  or or_4 (or_4_out, and_4_out, CLEAR);
  and and_4 (and_4_out, ~\mux_1_saída [3], ACTIVATE_PRESET);  // AND_Gate
endmodule

// DEC
module DECREMENTADOR (
  input  CLK,
  input  [3:0] PRESET,
  input  ACTIVATE_PRESET,
  input  ENABLE,
  input  CLEAR,
  output [3:0] \SAÍDA 
);

  wire [3:0] somador_1_sum;

  Hex_Digit_Display hex_digit_display_1 (.value(\SAÍDA ));  // open: dp
  REGISTRADOR registrador_1 (
    .D(somador_1_sum), .CLK(CLK), .PRESET(PRESET), .\SAÍDA (\SAÍDA ), .ENABLE(ENABLE),
    .ACTIVATE_PRESET(ACTIVATE_PRESET), .CLEAR(CLEAR));
  SOMADOR somador_1 (.A(\SAÍDA ), .B(4'b1111), .SUM(somador_1_sum));  // open: CARRY
  Hex_Digit_Display hex_digit_display_2 (.value(somador_1_sum));  // open: dp
endmodule

// CONT REG
module CONTADOR_REGRESSIVO (
  input  CLK,
  input  [3:0] PRESET_DM,
  input  ACTIVATE_PRESET,
  input  ENABLE,
  input  CLEAR,
  output [3:0] US,
  output [3:0] DS,
  output [3:0] UM,
  output [3:0] DM
);

  wire igual_1_out_3, igual_2_out_3, igual_3_out_3, igual_4_out_3, or_1_out, or_2_out, or_3_out, or_4_out;
  wire [3:0] \mux_1_saída , \mux_2_saída , \mux_3_saída , \mux_4_saída ;

  MUX mux_1 (.A(4'b0000), .B(4'b1001), .SELETOR(igual_1_out_3), .\SAÍDA (\mux_1_saída ));
  or or_1 (or_1_out, ACTIVATE_PRESET, igual_1_out_3);
  Hex_Digit_Display hex_digit_display_1 (.value(US));  // open: dp
  DECREMENTADOR decrementador_1 (
    .CLK(CLK), .PRESET(\mux_1_saída ), .ENABLE(ENABLE), .ACTIVATE_PRESET(or_1_out), .CLEAR(CLEAR),
    .\SAÍDA (US));
  IGUAL igual_1 (.out_3(igual_1_out_3), .A(US), .B(4'b1111));
  Hex_Digit_Display hex_digit_display_2 (.value(DS));  // open: dp
  MUX mux_2 (.A(4'b0000), .B(4'b0101), .SELETOR(igual_2_out_3), .\SAÍDA (\mux_2_saída ));
  or or_2 (or_2_out, ACTIVATE_PRESET, igual_2_out_3);
  DECREMENTADOR decrementador_2 (
    .CLK(igual_1_out_3), .PRESET(\mux_2_saída ), .ENABLE(ENABLE), .ACTIVATE_PRESET(or_2_out), .CLEAR(CLEAR),
    .\SAÍDA (DS));
  IGUAL igual_2 (.out_3(igual_2_out_3), .A(DS), .B(4'b1111));
  Hex_Digit_Display hex_digit_display_3 (.value(UM));  // open: dp
  MUX mux_3 (.A(4'b0000), .B(4'b1001), .SELETOR(igual_3_out_3), .\SAÍDA (\mux_3_saída ));
  or or_3 (or_3_out, ACTIVATE_PRESET, igual_3_out_3);
  DECREMENTADOR decrementador_3 (
    .CLK(igual_2_out_3), .PRESET(\mux_3_saída ), .ENABLE(ENABLE), .ACTIVATE_PRESET(or_3_out), .CLEAR(CLEAR),
    .\SAÍDA (UM));
  IGUAL igual_3 (.out_3(igual_3_out_3), .A(UM), .B(4'b1111));
  Hex_Digit_Display hex_digit_display_4 (.value(DM));  // open: dp
  or or_4 (or_4_out, ACTIVATE_PRESET, igual_4_out_3);
  DECREMENTADOR decrementador_4 (
    .CLK(igual_3_out_3), .PRESET(\mux_4_saída ), .ENABLE(ENABLE), .ACTIVATE_PRESET(or_4_out), .CLEAR(CLEAR),
    .\SAÍDA (DM));
  MUX mux_4 (.A(PRESET_DM), .B(4'b0101), .SELETOR(igual_4_out_3), .\SAÍDA (\mux_4_saída ));
  IGUAL igual_4 (.out_3(igual_4_out_3), .A(DM), .B(4'b1111));
endmodule

// =
module IGUAL (
  input  [3:0] A,
  input  [3:0] B,
  output out_3
);

  wire xnor_1_out, xnor_2_out, xnor_3_out, xnor_4_out;

  xnor xnor_1 (xnor_1_out, B[0], A[0]);
  xnor xnor_2 (xnor_2_out, B[1], A[1]);
  xnor xnor_3 (xnor_3_out, B[2], A[2]);
  xnor xnor_4 (xnor_4_out, B[3], A[3]);
  and and_1 (out_3, xnor_1_out, xnor_2_out, xnor_3_out, xnor_4_out);
endmodule

module CRONOMETRO (
  input  CLK,
  input  [3:0] PRESET_DM,
  input  ENABLE,
  input  ACTIVATE_PRESET,
  input  CLEAR,
  output [3:0] DM,
  output [3:0] UM,
  output [3:0] DS,
  output [3:0] US
);

  wire and_1_out, flip_flop_d_1_q, igual_1_out_3, igual_2_out_3, igual_3_out_3, igual_4_out_3,
       multiplexer_1_out;

  IGUAL igual_1 (.out_3(igual_1_out_3), .A(US), .B(4'b0000));
  IGUAL igual_2 (.out_3(igual_2_out_3), .A(DS), .B(4'b0000));
  IGUAL igual_3 (.out_3(igual_3_out_3), .A(UM), .B(4'b0000));
  IGUAL igual_4 (.out_3(igual_4_out_3), .A(DM), .B(4'b0000));
  and and_1 (and_1_out, igual_1_out_3, igual_2_out_3, igual_3_out_3, igual_4_out_3);
  Multiplexer #(.enable("false")) multiplexer_1 (
    .in0(ENABLE), .in1(flip_flop_d_1_q), .out(multiplexer_1_out), .sel(and_1_out));
  FLIP_FLOP_D flip_flop_d_1 (
    .D(1'b0), .CLK(and_1_out), .ENABLE(ENABLE), .PRESET(ACTIVATE_PRESET), .CLEAR(CLEAR), .Q(flip_flop_d_1_q));
  CONTADOR_REGRESSIVO contador_regressivo_1 (
    .CLK(CLK), .PRESET_DM(PRESET_DM), .US(US), .DS(DS), .UM(UM), .DM(DM), .ACTIVATE_PRESET(ACTIVATE_PRESET),
    .ENABLE(multiplexer_1_out), .CLEAR(CLEAR));
endmodule

module PRESET (
  input  CLK,
  input  CLEAR,
  output [3:0] \SAÍDA 
);

  wire igual_1_out_3;
  wire [3:0] \mux_1_saída , somador_1_sum;

  REGISTRADOR registrador_1 (
    .D(\mux_1_saída ), .CLK(CLK), .PRESET(4'b0000), .\SAÍDA (\SAÍDA ), .ENABLE(1'b1), .ACTIVATE_PRESET(1'b0),
    .CLEAR(CLEAR));
  SOMADOR somador_1 (.A(\SAÍDA ), .B(4'b0001), .SUM(somador_1_sum));  // open: CARRY
  IGUAL igual_1 (.out_3(igual_1_out_3), .A(somador_1_sum), .B(4'b0111));
  MUX mux_1 (.A(somador_1_sum), .B(4'b0001), .SELETOR(igual_1_out_3), .\SAÍDA (\mux_1_saída ));
endmodule
